# Fritzing sketch PCB-Design (saved by Fritzing 0.9.6b)
circuit board: 8.64595cm x 6.21431cm
breadboards: 1

parts:
  BUZZER = Piezo Speaker
  Part1 = Arduino Uno (Rev3)
  part = Header 6 [package=molex-1x6-ra]
  DHT11 = DHT11 basic temperature-humidity sensor [form="♂ (male)" package=THT]
  U1 = ESP8266 NodeMCU LoLin module
  FLAMESENSOR = Header 3 [package=screwterminal-3.5mm-3_lock.007s]
  LM393 = Header 4 [package=screwterminal-3.5mm-4_lock]

nets:
  N1: BUZZER.pin1, U1.D5
  5V: BUZZER.pin2, Part1.5V, part.6, DHT11.VCC, LM393.1
  GND: Part1.GND, part.1, DHT11.GND, U1.GND, FLAMESENSOR.2, LM393.2
  N2: part.2, U1.D8
  N3: part.3, U1.D2
  N4: part.4, U1.D1
  N5: DHT11.OUT, U1.D3
  N6: U1.D4, FLAMESENSOR.3
  N7: U1.3V3, FLAMESENSOR.1
  N8: U1.A0, LM393.4

notes:
  Ranganathaswamy Y S
  5v
  3.3v
  gnd
  OUTPUTS
  A0
  VCC
  D0
  GND
  KIT,Tiptur

custom parts:
  DHT11 basic temperature-humidity sensor: The DHT11 is a basic, ultra low-cost digital temperature and humidity sensor. It uses a capacitive humidity sensor and a thermistor to measure the surrounding air, and spits out a digital signal on the data pin (no analog input pins needed). Its fairly simple to use, but requires careful timing to grab data. The only real downside of this sensor is you can only get new data from it once every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
  ESP8266 NodeMCU LoLin module: ESP8266 based NodeMCU

// code stored in the sketch: Project_G.ino
#define CAYENNE_DEBUG
#define CAYENNE_PRINT Serial
#include <CayenneMQTTESP8266.h>
#include "DHT.h"
#define DHTTYPE DHT11
#define DHTPIN D3
#define valve1 D1
#define valve2 D2
#define flamePin D4
#define buzzer D5
#define moisturePin A0

char ssid[] = "Keerthi";
char wifiPassword[] = "12345678";

 
char username[] = "f6895170-c916-11eb-a2e4-b32ea624e442";
char password[] = "5461705d5593d7c76fb3ca09349df28091897ab7";
char clientID[] = "5bef1b80-c9c1-11eb-883c-638d8ce4c23d";

unsigned long lastMillis = 0;
int motor=D8;
int Flame=HIGH;
float moisturePercentage;
DHT dht(DHTPIN, DHTTYPE);
int FlameValue=0;


void setup() {
	Serial.begin(9600);
	Cayenne.begin(username, password, clientID, ssid, wifiPassword);
  dht.begin();
  pinMode(flamePin,INPUT);
  pinMode(motor,OUTPUT);
  pinMode(valve1,OUTPUT);
  pinMode(valve2,OUTPUT);
  pinMode(buzzer,OUTPUT);

  digitalWrite(motor,LOW);
  digitalWrite(buzzer,HIGH);  
  
}

void loop() {
	Cayenne.loop();
   float h = dht.readHumidity();
   float t = dht.readTemperature();
   moisturePercentage = ( 100.00 - ( (analogRead(moisturePin) / 1023.00) * 100.00 ));
   Flame=digitalRead(flamePin);
   if(Flame==HIGH){
    FlameValue=5;//random value for mapping high
    digitalWrite(buzzer,HIGH);
   }
   else if (Flame==LOW){
    FlameValue=8;
    digitalWrite(buzzer,LOW);}  // random value for low
   Cayenne.celsiusWrite(1, t);
   Cayenne.virtualWrite(2,h,TYPE_RELATIVE_HUMIDITY,UNIT_PERCENT);
   Cayenne.virtualWrite(3,moisturePercentage);
   Cayenne.virtualWrite(6,FlameValue);
   
  
}
CAYENNE_IN(0){

digitalWrite(motor,!getValue.asInt());
}

CAYENNE_IN(4){

digitalWrite(valve1,!getValue.asInt());
}

CAYENNE_IN(5){

digitalWrite(valve2,!getValue.asInt());
}

/*CAYENNE_IN(7){

digitalWrite(buzzer,!getValue.asInt());
}*/
