# Fritzing sketch swamy (saved by Fritzing 0.9.6b)
circuit board: 8.64595cm x 6.21431cm
breadboards: 1

parts:
  BUZZER = Piezo Speaker
  Part1 = Arduino Uno (Rev3)
  FlAME_SENSOR = KY-026
  LM393 = FC-28 Soil Hygrometer Module
  part = Header 6 [package=molex-1x6-ra]
  J1 = DHT11 basic temperature-humidity sensor [form="♂ (male)" package=THT]
  U1 = ESP8266 NodeMCU LoLin module

nets:
  N1: BUZZER.pin1, U1.D5
  VCC: BUZZER.pin2, Part1.5V, FlAME_SENSOR.pin3, LM393.VCC, part.6, J1.VCC
  GND: Part1.GND, FlAME_SENSOR.pin2, LM393.GND, part.1, J1.GND, U1.GND
  N2: FlAME_SENSOR.pin4, U1.D4
  N3: LM393.AO, U1.A0
  N4: part.2, U1.D8
  N5: part.3, part.5, U1.D2
  N6: part.4, U1.D1
  N7: J1.OUT, U1.D3

notes:
  Ranganathaswamy Y S
  DHT11
  5v
  3.3v
  gnd
  OUTPUTS
  A0
  +
  -
  S

custom parts:
  KY-026: ky-026 flame sensor module
  FC-28 Soil Hygrometer Module: The FC-28 is a soil hygrometer module that uses the Texas Instruments LM393 comparator chip to provide an analog measurement of soil humidity. The digital output is high when soil moisture is over a certain threshold, as determined by adjusting the potentiometer.
  DHT11 basic temperature-humidity sensor: The DHT11 is a basic, ultra low-cost digital temperature and humidity sensor. It uses a capacitive humidity sensor and a thermistor to measure the surrounding air, and spits out a digital signal on the data pin (no analog input pins needed). Its fairly simple to use, but requires careful timing to grab data. The only real downside of this sensor is you can only get new data from it once every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
  ESP8266 NodeMCU LoLin module: ESP8266 based NodeMCU

// code stored in the sketch: Project_G.ino
#define CAYENNE_DEBUG
#define CAYENNE_PRINT Serial
#include <CayenneMQTTESP8266.h>
#include "DHT.h"
#define DHTTYPE DHT11
#define DHTPIN D3
#define valve1 D1
#define valve2 D2
#define flamePin D4
#define buzzer D5
#define moisturePin A0

char ssid[] = "Keerthi";
char wifiPassword[] = "12345678";

 
char username[] = "f6895170-c916-11eb-a2e4-b32ea624e442";
char password[] = "5461705d5593d7c76fb3ca09349df28091897ab7";
char clientID[] = "5bef1b80-c9c1-11eb-883c-638d8ce4c23d";

unsigned long lastMillis = 0;
int motor=D8;
int Flame=HIGH;
float moisturePercentage;
DHT dht(DHTPIN, DHTTYPE);
int FlameValue=0;


void setup() {
	Serial.begin(9600);
	Cayenne.begin(username, password, clientID, ssid, wifiPassword);
  dht.begin();
  pinMode(flamePin,INPUT);
  pinMode(motor,OUTPUT);
  pinMode(valve1,OUTPUT);
  pinMode(valve2,OUTPUT);
  pinMode(buzzer,OUTPUT);

  digitalWrite(motor,LOW);
  digitalWrite(buzzer,HIGH);  
  
}

void loop() {
	Cayenne.loop();
   float h = dht.readHumidity();
   float t = dht.readTemperature();
   moisturePercentage = ( 100.00 - ( (analogRead(moisturePin) / 1023.00) * 100.00 ));
   Flame=digitalRead(flamePin);
   if(Flame==HIGH){
    FlameValue=5;//random value for mapping high
    digitalWrite(buzzer,HIGH);
   }
   else if (Flame==LOW){
    FlameValue=8;
    digitalWrite(buzzer,LOW);}  // random value for low
   Cayenne.celsiusWrite(1, t);
   Cayenne.virtualWrite(2,h,TYPE_RELATIVE_HUMIDITY,UNIT_PERCENT);
   Cayenne.virtualWrite(3,moisturePercentage);
   Cayenne.virtualWrite(6,FlameValue);
   
  
}
CAYENNE_IN(0){

digitalWrite(motor,!getValue.asInt());
}

CAYENNE_IN(4){

digitalWrite(valve1,!getValue.asInt());
}

CAYENNE_IN(5){

digitalWrite(valve2,!getValue.asInt());
}

/*CAYENNE_IN(7){

digitalWrite(buzzer,!getValue.asInt());
}*/
